// Logisim project cmos.circ as structural Verilog: 4 circuits, main circuit cmos_inv
module cmos_inv (
  input  A,
  output Y
);

  Transistor #(.\type ("p")) transistor_1 (.in(1'b1), .out(Y), .gate(A));
  Transistor #(.\type ("n")) transistor_2 (.in(1'b0), .out(Y), .gate(A));
endmodule

module cmos_nand (
  input  A,
  input  B,
  output Y
);

  wire n1;

  Transistor #(.\type ("n")) transistor_1 (.in(1'b0), .out(n1), .gate(A));
  Transistor #(.\type ("n")) transistor_2 (.in(n1), .out(Y), .gate(B));
  Transistor #(.\type ("p")) transistor_3 (.in(1'b1), .out(Y), .gate(A));
  Transistor #(.\type ("p")) transistor_4 (.in(1'b1), .out(Y), .gate(B));
endmodule

module tgate_mux (
  input  S,
  input  D0,
  input  D1,
  output Y
);

  wire Sn;

  not not_1 (Sn, S);
  // Transmission_Gate transmission_1: pin names not known; wires that end beside it: D1, Sn, S, Y
  // Transmission_Gate transmission_2: pin names not known; wires that end beside it: D0, S, Sn, Y
endmodule

module pseudo_nor (
  input  A,
  input  B,
  output Y
);

  Transistor #(.\type ("n")) transistor_1 (.in(1'b0), .out(Y), .gate(A));
  Transistor #(.\type ("n")) transistor_2 (.in(1'b0), .out(Y), .gate(B));
  Pull_Resistor #(.pull(1)) pull_resistor_1 (.node(Y));
endmodule
