// Logisim project full_adder.circ as structural Verilog: 1 circuit, main circuit full_adder
module full_adder (
  input  A,
  input  B,
  input  Cin,
  output S,
  output Cout
);

  wire _t1, _t2, AxB;

  and and_1 (_t2, Cin, AxB);
  or or_1 (Cout, _t1, _t2);
  xor xor_1 (AxB, A, B);
  xor xor_2 (S, AxB, Cin);
  and and_2 (_t1, A, B);
endmodule
